# Fritzing sketch Untitled Sketch (saved by Fritzing 0.9.3b)

parts:
  U1 = NodeMCU V1.0
  U2 = LM2596 step down module
  Part1 = FC-28 Soil Hygrometer Module
  Part2 = FC-28 Soil Hygrometer Module - Probe
  KY-1 = Keyes Relay [package=THT]
  YF-S201_Flow_Meter1 = YF-S201 Water Flow Meter
  DHT1 = DHT22 Humidity and Temperature Sensor

nets:
  N1: U1.D1, U1.D5, DHT1.VDD
  N2: U1.D2, KY-1.power
  VIN: U1.Vin, Part1.VCC, KY-1.signal, DHT1.DATA
  GND: U1.GND, U2.IN-, U2.OUT-, Part1.GND, KY-1.ground, DHT1.NULL
  N3: U1.A0, Part1.AO
  N4: Part1.POS, Part2.POS
  N5: Part1.NEG, Part2.NEG
  N6: KY-1.NC, YF-S201_Flow_Meter1.SIG

custom parts:
  NodeMCU V1.0: ESP8266 based NodeMCU V1.0
  LM2596 step down module: LM2596 DC-DC step down power supply module 3 A.
  FC-28 Soil Hygrometer Module: The FC-28 is a soil hygrometer module that uses the Texas Instruments LM393 comparator chip to provide an analog measurement of soil humidity. The digital output is high when soil moisture is over a certain threshold, as determined by adjusting the potentiometer.
  FC-28 Soil Hygrometer Module - Probe: The FC-28 is a soil hygrometer module that uses the Texas Instruments LM393 comparator chip to provide an analog measurement of soil humidity.
  Keyes Relay: The Keyes 5V relay module is suitable for SCM development, home appliance control. It uses a 5V~12V TIL control signal which can control DC / AC signal.
  YF-S201 Water Flow Meter: The YF-S201 Flow Meter. The input voltage is 5V to 24V (DC).
